# Fritzing sketch osl_sensors (saved by Fritzing 0.8.3b)
circuit board: 6.88561cm x 5.36311cm
breadboards: 1

parts:
  HIH-4030 = Humidity Sensor - HIH-4030 Breakout
  OSL_Oct_2013 = Arduino Leonardo (Rev3b)
  R1 = Resistor [tolerance=±1% resistance=22k package=THT]
  R2 = Resistor [tolerance=±1% resistance=22k package=THT]
  R3 = Resistor [tolerance=±1% resistance=22k package=THT]
  R4 = Resistor [tolerance=±1% resistance=22k package=THT]
  R5 = Resistor [tolerance=±1% resistance=2.2k package=THT]
  R6 = Resistor [tolerance=±1% resistance=2.2k package=THT]
  R7 = Resistor [tolerance=±1% resistance=2.2k package=THT]
  R8 = Resistor [tolerance=±1% resistance=2.2k package=THT]
  MAX485 = MAX485 [package=dil08]
  J1 = double row male pin header, 6 pins [form="♂ (male)"]
  BMP-085 = Barometric Pressure Sensor - BMP085 Breakout
  R9 = Resistor [tolerance=±1% resistance=150 package=THT]
  J2 = molex pin header, 3 pins [form=molex]
  J3 = molex pin header, 3 pins [form=molex]
  J4 = molex pin header, 4 pins [form=molex]
  J5 = molex pin header, 3 pins [form=molex]
  J6 = molex pin header, 3 pins [form=molex]
  I2C = molex pin header, 2 pins [form=molex]
  UART = molex pin header, 2 pins [form=molex]
  RS485 = molex pin header, 2 pins [form=molex]

nets:
  GND: HIH-4030.GND, OSL_Oct_2013.GND, R5.Pin_1, R6.Pin_1, R7.Pin_1, R8.Pin_1, MAX485.GND, BMP-085.GND, J2.pin3, J3.pin3, J5.pin3, J6.pin3
  N1: HIH-4030.OUT, OSL_Oct_2013.D4/A6
  VCC: HIH-4030.VCC, OSL_Oct_2013.IOREF, OSL_Oct_2013.5V, MAX485.VCC, J2.pin1, J3.pin1, J5.pin1, J6.pin1
  N2: OSL_Oct_2013.D0/RX, J1.pin2
  N3: OSL_Oct_2013.D1/TX, J1.pin5
  N4: OSL_Oct_2013.D2/SDA, OSL_Oct_2013.SDA, BMP-085.SDA, I2C.pin2
  N5: OSL_Oct_2013.D3_PWM/SCL, OSL_Oct_2013.SCL, BMP-085.SCL, I2C.pin1
  N6: OSL_Oct_2013.D7, MAX485.RE, MAX485.DE
  3V3: OSL_Oct_2013.3V3, BMP-085.VCC
  N7: OSL_Oct_2013.A0, R1.Pin_1, R5.Pin_0
  N8: OSL_Oct_2013.A1, R2.Pin_1, R6.Pin_0
  N9: OSL_Oct_2013.A2, R3.Pin_1, R7.Pin_0
  N10: OSL_Oct_2013.A3, R4.Pin_1, R8.Pin_0
  N11: OSL_Oct_2013.A4, J2.pin2
  N12: OSL_Oct_2013.A5, J3.pin2
  N13: OSL_Oct_2013.D8/A8, J6.pin2
  N14: OSL_Oct_2013.D12/A11, J5.pin2
  N15: R1.Pin_0, J4.pin1
  N16: R2.Pin_0, J4.pin2
  N17: R3.Pin_0, J4.pin3
  N18: R4.Pin_0, J4.pin4
  N19: MAX485.RO, J1.pin1
  N20: MAX485.DI, J1.pin6
  N21: MAX485.A, R9.Pin_1, RS485.pin1
  N22: MAX485.B, R9.Pin_0, RS485.pin2
  N23: J1.pin3, UART.pin1
  N24: J1.pin4, UART.pin2

notes:
  Nessie Sensors PCB
